// Digital circuit ALU completa.dig as structural Verilog
module ALU_completa (
  input  A0,
  input  A1,
  input  A2,
  input  A3,
  input  A4,
  input  A5,
  input  A6,
  input  A7,
  input  B0,
  input  B1,
  input  B2,
  input  B3,
  input  B4,
  input  B5,
  input  B6,
  input  B7,
  input  _0,
  input  _1,
  input  _2
);

  wire CoutL, CoutM, CoutS, CoutSub, multiplexer_2_out;
  wire [7:0] And, Left, Mult, multiplexer_1_out, Or, Right, Soma, Sub, Xor;

  // xor xor_1: pin names not known; wires that end beside it: A0, A1, A2, A3, A4, A5, A6, A7, B0, B1, B2, B3, B4, B5, Xor
  // or or_1: pin names not known; wires that end beside it: B6, B7, A0, A1, A2, A3, A4, A5, A6, A7, B0, B1, B2, B3, B4, B5, Or
  // and and_1: pin names not known; wires that end beside it: B6, B7, A0, A1, A2, A3, A4, A5, A6, A7, B0, B1, B2, B3, B4, B5, B6, B7, And
  somador8bit somador8bit_1 (
    .A0(A0), .A1(A1), .A2(A2), .A3(A3), .A4(A4), .A5(A5), .A6(A6), .A7(A7), .B0(B0), .B1(B1), .B2(B2),
    .B3(B3), .B4(B4), .B5(B5), .B6(B6), .B7(B7), .Cin(1'b0), .Cout(CoutS), .S(Soma));
  subtrator8bit subtrator8bit_1 (
    .A0(A0), .A1(A1), .A2(A2), .A3(A3), .A4(A4), .A5(A5), .A6(A6), .A7(A7), .B0(B0), .B1(B1), .B2(B2),
    .B3(B3), .B4(B4), .B5(B5), .B6(B6), .B7(B7), .Cout(CoutSub), .Sub(Sub));
  mult mult_1 (
    .A0(A0), .A1(A1), .A2(A2), .A3(A3), .B0(B0), .B1(B1), .B2(B2), .B3(B3), .Multiplicador(Mult),
    .Overflow(CoutM));
  // rightShift rightshift_1: pin names not known; wires that end beside it: A0, A1, A2, A3, A4, A5, A6, A7, Right
  // leftShift leftshift_1: pin names not known; wires that end beside it: A0, A1, A2, A3, A4, A5, A6, A7, Left, CoutL
  Multiplexer #(.Selector_Bits(3), .Bits(8)) multiplexer_1 (
    .sel({_2, _1, _0}), .in_0(Soma), .in_1(Sub), .in_2(Mult), .in_3(Right), .in_4(Left), .in_5(And),
    .in_6(Or), .in_7(Xor), .out(multiplexer_1_out));
  Multiplexer #(.Selector_Bits(3)) multiplexer_2 (
    .sel({_2, _1, _0}), .in_0(CoutS), .in_1(CoutSub), .in_2(CoutM), .in_3(1'b0), .in_4(CoutL), .in_5(1'b0),
    .in_6(1'b0), .in_7(1'b0), .out(multiplexer_2_out));
  LED led_1 (.in(multiplexer_2_out));
  Seven_Seg_Hex seven_seg_hex_1 (.d(multiplexer_1_out[7:4]), .dp(1'b0));
  Seven_Seg_Hex seven_seg_hex_2 (.d(multiplexer_1_out[3:0]), .dp(1'b0));

  // Other names for the same wires on the sheet: Sel[2:0] = {_2, _1, _0}
endmodule
