// Digital circuit ALU-CPU.dig as structural Verilog
module ALU_CPU (
  input  _0,
  input  _1,
  input  _2,
  input  [7:0] A,
  input  [7:0] B,
  output OF,
  output [7:0] S_ALU
);

  wire CoutL, CoutM, CoutS, CoutSub;
  wire [7:0] And, Left, Mult, Or, Right, Soma, Sub, Xor;

  // xor xor_1: pin names not known; wires that end beside it: A[0], A[1], A[2], A[3], A[4], A[5], A[6], A[7], B[0], B[1], B[2], B[3], B[4], B[5], Xor
  // or or_1: pin names not known; wires that end beside it: B[6], B[7], A[0], A[1], A[2], A[3], A[4], A[5], A[6], A[7], B[0], B[1], B[2], B[3], B[4], B[5], Or
  // and and_1: pin names not known; wires that end beside it: B[6], B[7], A[0], A[1], A[2], A[3], A[4], A[5], A[6], A[7], B[0], B[1], B[2], B[3], B[4], B[5], B[6], B[7], And
  somador8bit somador8bit_1 (
    .A0(A[0]), .A1(A[1]), .A2(A[2]), .A3(A[3]), .A4(A[4]), .A5(A[5]), .A6(A[6]), .A7(A[7]), .B0(B[0]),
    .B1(B[1]), .B2(B[2]), .B3(B[3]), .B4(B[4]), .B5(B[5]), .B6(B[6]), .B7(B[7]), .Cin(1'b0), .Cout(CoutS),
    .S(Soma));
  subtrator8bit subtrator8bit_1 (
    .A0(A[0]), .A1(A[1]), .A2(A[2]), .A3(A[3]), .A4(A[4]), .A5(A[5]), .A6(A[6]), .A7(A[7]), .B0(B[0]),
    .B1(B[1]), .B2(B[2]), .B3(B[3]), .B4(B[4]), .B5(B[5]), .B6(B[6]), .B7(B[7]), .Cout(CoutSub), .Sub(Sub));
  multiplicador4bit multiplicador4bit_1 (
    .A0(A[0]), .B0(B[0]), .A1(A[1]), .B1(B[1]), .A2(A[2]), .B2(B[2]), .A3(A[3]), .B3(B[3]), .M(Mult),
    .Overflow(CoutM));
  // rightShift rightshift_1: pin names not known; wires that end beside it: A[0], A[1], A[2], A[3], A[4], A[5], A[6], A[7], Right
  // leftShift leftshift_1: pin names not known; wires that end beside it: A[0], A[1], A[2], A[3], A[4], A[5], A[6], A[7], Left, CoutL
  Multiplexer #(.Selector_Bits(3), .Bits(8)) multiplexer_1 (
    .sel({_2, _1, _0}), .in_0(Soma), .in_1(Sub), .in_2(Mult), .in_3(Right), .in_4(Left), .in_5(And),
    .in_6(Or), .in_7(Xor), .out(S_ALU));
  Multiplexer #(.Selector_Bits(3)) multiplexer_2 (
    .sel({_2, _1, _0}), .in_0(CoutS), .in_1(CoutSub), .in_2(CoutM), .in_3(1'b0), .in_4(CoutL), .in_5(1'b0),
    .in_6(1'b0), .in_7(1'b0), .out(OF));
  // Pins of 1 and 8 bits meet at S_ALU

  // Other names for the same wires on the sheet: Sel[2:0] = {_2, _1, _0}
endmodule
