// Digital circuit CPU.dig as structural Verilog
module CPU (
  input  clk
);

  wire alu_cpu_1_p6, counter_1_ovf, RESETAR_out, Sel0, Sel1, Sel2;
  wire [1:0] counter_1_out;
  wire [7:0] A, B, S;

  Register #(.Bits(8)) register_1 (.D(S), .C(clk), .en(1'b1), .Q(A));
  Button RESETAR (.out(RESETAR_out));
  Counter #(.Bits(2)) counter_1 (.en(1'b1), .C(clk), .clr(RESETAR_out), .out(counter_1_out), .ovf(counter_1_ovf));
  LED led_1 (.in(counter_1_ovf));
  Seven_Seg_Hex seven_seg_hex_1 (.d(A[7:4]), .dp(1'b0));
  Seven_Seg_Hex seven_seg_hex_2 (.d(A[3:0]), .dp(1'b0));
  ROM #(.Bits(11)) rom_1 (.A(counter_1_out), .sel(1'b1), .D({B, Sel2, Sel1, Sel0}));
  // ALU_CPU alu_cpu_1: pin names not known; wires that end beside it: Sel0, Sel1, Sel2, A, B, alu_cpu_1_p6, S
  LED led_2 (.in(alu_cpu_1_p6));

  // Notes on the sheet:
  //   contents of rom_1 (hex, n*v repeats v):
  //   50,12,c,7d
endmodule
