// Digital circuit leftShift.dig as structural Verilog
module leftShift (
  input  A0,
  input  A1,
  input  A2,
  input  A3,
  input  A4,
  input  A5,
  input  A6,
  input  A7,
  output [7:0] L,
  output Cout
);

  // Pins of 1 and 8 bits meet at {A6, A5, A4, A3, A2, A1, A0, 1'b0}

  assign Cout = 1'b0;
  assign L = {A6, A5, A4, A3, A2, A1, A0, 1'b0};
endmodule
