// Digital circuit mult.dig as structural Verilog
module mult (
  input  A0,
  input  A1,
  input  A2,
  input  A3,
  input  B0,
  input  B1,
  input  B2,
  input  B3,
  output [7:0] Multiplicador,
  output Overflow
);

  wire and_1_out, and_2_out, and_3_out, and_5_out, and_6_out, and_7_out, and_8_out, and_9_out, and_10_out,
       and_11_out, and_12_out, and_13_out, and_14_out, and_15_out, and_16_out, meiosomador_1_carry,
       meiosomador_2_carry, meiosomador_3_carry, meiosomador_4_carry, somadorc_1_cout, somadorc_1_s,
       somadorc_2_cout, somadorc_2_s, somadorc_3_cout, somadorc_3_s, somadorc_4_cout, somadorc_4_s,
       somadorc_5_cout, somadorc_5_s, somadorc_6_cout, somadorc_6_s, somadorc_7_s;

  and and_1 (and_1_out, A0, B2);
  and and_2 (and_2_out, A0, B3);
  and and_3 (and_3_out, A0, B1);
  and and_4 (Multiplicador[0], A0, B0);
  and and_5 (and_5_out, A1, B1);
  and and_6 (and_6_out, A1, B2);
  and and_7 (and_7_out, A1, B3);
  and and_8 (and_8_out, A1, B0);
  and and_9 (and_9_out, A2, B2);
  and and_10 (and_10_out, A2, B3);
  and and_11 (and_11_out, A2, B0);
  and and_12 (and_12_out, A2, B1);
  and and_13 (and_13_out, A3, B1);
  and and_14 (and_14_out, A3, B2);
  and and_15 (and_15_out, A3, B3);
  and and_16 (and_16_out, A3, B0);
  meioSomador meiosomador_1 (.A(and_8_out), .B(and_3_out), .Soma(Multiplicador[1]), .Carry(meiosomador_1_carry));
  somadorC somadorc_1 (
    .A(meiosomador_1_carry), .B(and_11_out), .Cin(and_5_out), .Cout(somadorc_1_cout), .S(somadorc_1_s));
  meioSomador meiosomador_2 (.A(somadorc_1_cout), .B(and_1_out), .Soma(Multiplicador[2]), .Carry(meiosomador_2_carry));
  somadorC somadorc_2 (.A(somadorc_1_s), .B(and_16_out), .Cin(and_12_out), .Cout(somadorc_2_cout), .S(somadorc_2_s));
  somadorC somadorc_3 (
    .A(meiosomador_2_carry), .B(somadorc_2_cout), .Cin(and_6_out), .Cout(somadorc_3_cout), .S(somadorc_3_s));
  meioSomador meiosomador_3 (.A(somadorc_3_cout), .B(and_2_out), .Soma(Multiplicador[3]), .Carry(meiosomador_3_carry));
  somadorC somadorc_4 (.A(somadorc_2_s), .B(and_13_out), .Cin(and_9_out), .Cout(somadorc_4_cout), .S(somadorc_4_s));
  somadorC somadorc_5 (
    .A(somadorc_3_s), .B(somadorc_4_cout), .Cin(and_7_out), .Cout(somadorc_5_cout), .S(somadorc_5_s));
  somadorC somadorc_6 (.A(somadorc_4_s), .B(and_14_out), .Cin(and_10_out), .Cout(somadorc_6_cout), .S(somadorc_6_s));
  meioSomador meiosomador_4 (
    .A(somadorc_5_cout), .B(meiosomador_3_carry), .Soma(Multiplicador[4]), .Carry(meiosomador_4_carry));
  somadorC somadorc_7 (
    .A(meiosomador_4_carry), .B(somadorc_6_cout), .Cin(somadorc_5_s), .Cout(Multiplicador[5]),
    .S(somadorc_7_s));
  somadorC somadorc_8 (
    .A(somadorc_7_s), .B(and_15_out), .Cin(somadorc_6_s), .Cout(Multiplicador[6]), .S(Multiplicador[7]));
  or or_1 (Overflow, Multiplicador[4], Multiplicador[5], Multiplicador[6], Multiplicador[7]);

  // Notes on the sheet:
  //   A0·B2
  //   A0·B3
  //   A0·B0
  //   A0·B1
  //   A1·B1
  //   A1·B2
  //   A1·B3
  //   A1·B0
  //   A2·B2
  //   A2·B3
  //   A2·B0
  //   A2·B1
  //   A3·B1
  //   A3·B2
  //   A3·B3
  //   A3·B0
  //   MULTIPLICADOR DE 8 BITS
endmodule
