// Digital circuit multiplicador4bit.dig as structural Verilog
module multiplicador4bit (
  input  A0,
  input  B0,
  input  A1,
  input  B1,
  input  A2,
  input  B2,
  input  A3,
  input  B3,
  output [7:0] M,
  output Overflow
);

  wire Cout1, Cout2, Cout3, Cout4, Cout5, Cout6, Cout7, Cout8, Cout9, Cout10, Cout11, P0_1, P0_2, P0_3, P1_0,
       P1_1, P1_2, P1_3, P2_0, P2_1, P2_2, P2_3, P3_0, P3_1, P3_2, P3_3, S2, S4, S5, S7, S8, S10;

  and and_1 (M[0], A0, B0);
  and and_2 (P1_0, A1, B0);
  and and_3 (P2_0, A2, B0);
  and and_4 (P3_0, A3, B0);
  and and_5 (P0_1, A0, B1);
  and and_6 (P1_1, A1, B1);
  and and_7 (P2_1, A2, B1);
  and and_8 (P3_1, A3, B1);
  and and_9 (P0_2, A0, B2);
  and and_10 (P1_2, A1, B2);
  and and_11 (P2_2, A2, B2);
  and and_12 (P3_2, A3, B2);
  and and_13 (P0_3, A0, B3);
  and and_14 (P1_3, A1, B3);
  and and_15 (P2_3, A2, B3);
  and and_16 (P3_3, A3, B3);
  meioSomador _1 (.A(P1_0), .B(P0_1), .Soma(M[1]), .Carry(Cout1));
  somadorC _2 (.A(P2_0), .B(P2_1), .Cin(Cout1), .Cout(Cout2), .S(S2));
  meioSomador _3 (.A(S2), .B(P0_2), .Soma(M[2]), .Carry(Cout3));
  somadorC _4 (.A(P3_0), .B(P2_1), .Cin(Cout2), .Cout(Cout4), .S(S4));
  somadorC _5 (.A(S4), .B(P1_2), .Cin(Cout3), .Cout(Cout5), .S(S5));
  meioSomador _6 (.A(S5), .B(P0_3), .Soma(M[3]), .Carry(Cout6));
  somadorC _7 (.A(P3_1), .B(P2_2), .Cin(Cout4), .Cout(Cout7), .S(S7));
  somadorC _8 (.A(S7), .B(P1_3), .Cin(Cout5), .Cout(Cout8), .S(S8));
  meioSomador _9 (.A(S8), .B(Cout6), .Soma(M[4]), .Carry(Cout9));
  somadorC _10 (.A(P3_2), .B(P2_3), .Cin(Cout6), .Cout(Cout10), .S(S10));
  somadorC _11 (.A(S10), .B(Cout8), .Cin(Cout9), .Cout(Cout11), .S(M[5]));
  somadorC _12 (.A(P3_3), .B(Cout10), .Cin(Cout11), .Cout(M[7]), .S(M[6]));
  or or_1 (Overflow, M[4], M[5], M[6], M[7]);

  // Other names for the same wires on the sheet: Cout12 = M[7]; P0_0 = M[0]; S1 = M[1]; S3 = M[2]; S6 = M[3];
  //   S9 = M[4]; S11 = M[5]; S12 = M[6]
endmodule
