// Digital circuit rightShift.dig as structural Verilog
module rightShift (
  input  A0,
  input  A1,
  input  A2,
  input  A3,
  input  A4,
  input  A5,
  input  A6,
  input  A7,
  output [7:0] R
);

  // Pins of 1 and 8 bits meet at {1'b0, A7, A6, A5, A4, A3, A2, A1}

  assign R = {1'b0, A7, A6, A5, A4, A3, A2, A1};
endmodule
