// Digital circuit somador8bit.dig as structural Verilog
module somador8bit (
  input  A0,
  input  A1,
  input  A2,
  input  A3,
  input  A4,
  input  A5,
  input  A6,
  input  A7,
  input  B0,
  input  B1,
  input  B2,
  input  B3,
  input  B4,
  input  B5,
  input  B6,
  input  B7,
  input  Cin,
  output Cout,
  output [7:0] S
);

  _4_bit _4_bit_1 (
    .A0(A0), .B0(B0), .A1(A1), .B1(B1), .A2(A2), .B2(B2), .A3(A3), .B3(B3), .A4(A4), .B4(B4), .A5(A5),
    .B5(B5), .A6(A6), .B6(B6), .A7(A7), .B7(B7), .Cin(Cin), .S0(S[0]), .S1(S[1]), .S2(S[2]), .S3(S[3]),
    .S4(S[4]), .S5(S[5]), .S6(S[6]), .S7(S[7]), .Cout(Cout));
endmodule
