// Digital circuit subtrator8bit.dig as structural Verilog
module subtrator8bit (
  input  A0,
  input  A1,
  input  A2,
  input  A3,
  input  A4,
  input  A5,
  input  A6,
  input  A7,
  input  B0,
  input  B1,
  input  B2,
  input  B3,
  input  B4,
  input  B5,
  input  B6,
  input  B7,
  output Cout,
  output [7:0] Sub
);

  wire xor_1_out, xor_2_out, xor_3_out, xor_4_out, xor_5_out, xor_6_out, xor_7_out, xor_8_out;

  xor xor_1 (xor_1_out, B0, 1'b1);
  xor xor_2 (xor_2_out, B1, 1'b1);
  xor xor_3 (xor_3_out, B2, 1'b1);
  xor xor_4 (xor_4_out, B3, 1'b1);
  xor xor_5 (xor_5_out, B4, 1'b1);
  xor xor_6 (xor_6_out, B5, 1'b1);
  xor xor_7 (xor_7_out, B6, 1'b1);
  xor xor_8 (xor_8_out, B7, 1'b1);
  _4_bit _4_bit_1 (
    .A0(A0), .B0(xor_1_out), .A1(A1), .B1(xor_2_out), .A2(A2), .B2(xor_3_out), .A3(A3), .B3(xor_4_out),
    .A4(A4), .B4(xor_5_out), .A5(A5), .B5(xor_6_out), .A6(A6), .B6(xor_7_out), .A7(A7), .B7(xor_8_out),
    .Cin(1'b1), .S0(Sub[0]), .S1(Sub[1]), .S2(Sub[2]), .S3(Sub[3]), .S4(Sub[4]), .S5(Sub[5]), .S6(Sub[6]),
    .S7(Sub[7]), .Cout(Cout));
endmodule
