// Digital circuit xor.dig as structural Verilog
module \xor  (
  input  A0,
  input  A1,
  input  A2,
  input  A3,
  input  A4,
  input  A5,
  input  A6,
  input  A7,
  input  B0,
  input  B1,
  input  B2,
  input  B3,
  input  B4,
  input  B5,
  input  B6,
  input  B7,
  output [7:0] So
);

  xor xor_1 (So[0], A0, B0);
  xor xor_2 (So[1], A1, B1);
  xor xor_3 (So[2], A2, B2);
  xor xor_4 (So[3], A3, B3);
  xor xor_5 (So[4], A4, B4);
  xor xor_6 (So[5], A5, B5);
  xor xor_7 (So[6], A6, B6);
  xor xor_8 (So[7], A7, B7);
  // Pins of 1 and 8 bits meet at So
endmodule
